// Logisim project trabalho.circ as structural Verilog: 4 circuits, main circuit main
module main (
  input  in_1,
  input  in_2,
  input  in_3,
  input  in_4,
  input  in_5,
  input  in_6,
  input  in_7,
  input  in_8,
  input  in_9,
  input  in_10,
  input  in_11,
  input  in_12,
  input  in_13,
  input  in_14
);

  wire [3:0] coder_2_u, coder_u;

  Hex_Digit_Display hex_digit_display_1 (.value(coder_2_u));  // open: dp
  Hex_Digit_Display hex_digit_display_2 (.value(coder_u));  // open: dp
  coder coder (
    .a(in_8), .b(in_9), .c(in_10), .d(in_13), .e(in_12), .f(in_14), .g(in_11), .x(coder_u[3]),
    .y(coder_u[2]), .z(coder_u[1]), .u(coder_u[0]));
  coder coder_2 (
    .a(in_1), .b(in_2), .c(in_3), .d(in_6), .e(in_5), .f(in_7), .g(in_4), .x(coder_2_u[3]), .y(coder_2_u[2]),
    .z(coder_2_u[1]), .u(coder_2_u[0]));
  calculadora calculadora_1 ();  // open: num_1, num_2, Seletor_1, Seletor_2, out_5
endmodule

// Somador
module somador (
  input  A,
  input  B,
  input  Ci,
  output S,
  output Co
);

  wire and_1_out, and_2_out, and_3_out, and_4_out, and_5_out, and_6_out, and_7_out, not_1_out, not_2_out,
       not_3_out, not_4_out, not_5_out, not_6_out;

  not not_1 (not_1_out, B);
  not not_2 (not_2_out, Ci);
  not not_3 (not_3_out, A);
  not not_4 (not_4_out, Ci);
  not not_5 (not_5_out, A);
  not not_6 (not_6_out, B);
  and and_1 (and_1_out, A, not_1_out, not_2_out);
  and and_2 (and_2_out, A, B, Ci);
  and and_3 (and_3_out, not_3_out, B, not_4_out);
  and and_4 (and_4_out, not_5_out, not_6_out, Ci);
  and and_5 (and_5_out, A, Ci);
  and and_6 (and_6_out, A, B);
  and and_7 (and_7_out, B, Ci);
  or or_1 (S, and_1_out, and_2_out, and_3_out, and_4_out);
  or or_2 (Co, and_5_out, and_6_out, and_7_out);
endmodule

module coder (
  input  a,
  input  b,
  input  c,
  input  d,
  input  e,
  input  f,
  input  g,
  output x,
  output y,
  output z,
  output u
);

  wire and_1_out, and_2_out, and_3_out, and_4_out, and_5_out, and_6_out, and_7_out, and_8_out, and_9_out,
       and_10_out, and_11_out, and_12_out, and_13_out, not_1_out, not_2_out, not_3_out, not_4_out, not_5_out,
       not_6_out, not_7_out, not_8_out, not_9_out, not_10_out, not_11_out, not_12_out, not_13_out,
       not_14_out, not_15_out, not_16_out;

  not not_1 (not_1_out, c);
  not not_2 (not_2_out, d);
  not not_3 (not_3_out, b);
  not not_4 (not_4_out, b);
  not not_5 (not_5_out, c);
  not not_6 (not_6_out, e);
  not not_7 (not_7_out, g);
  not not_8 (not_8_out, c);
  not not_9 (not_9_out, f);
  not not_10 (not_10_out, a);
  not not_11 (not_11_out, b);
  not not_12 (not_12_out, c);
  not not_13 (not_13_out, c);
  not not_14 (not_14_out, f);
  not not_15 (not_15_out, a);
  not not_16 (not_16_out, e);
  and and_1 (and_1_out, not_1_out, not_2_out);
  and and_2 (and_2_out, not_3_out, f);
  and and_3 (and_3_out, a, b, c, g);
  and and_4 (and_4_out, not_4_out, c, g);
  and and_5 (and_5_out, b, not_5_out);
  and and_6 (and_6_out, b, not_6_out, not_7_out);
  and and_7 (and_7_out, not_8_out, f, g);
  and and_8 (and_8_out, c, e, not_9_out);
  and and_9 (and_9_out, not_10_out, b);
  and and_10 (and_10_out, not_11_out, not_12_out);
  and and_11 (and_11_out, not_13_out, not_14_out);
  and and_12 (and_12_out, not_15_out, d);
  and and_13 (and_13_out, b, not_16_out);
  or or_1 (x, and_1_out, and_2_out, and_3_out);
  or or_2 (y, and_4_out, and_5_out, and_6_out);
  or or_3 (z, and_7_out, and_8_out, and_9_out);
  or or_4 (u, and_10_out, and_11_out, and_12_out, and_13_out);
endmodule

module calculadora (
  input  num_1,
  input  num_2,
  input  Seletor_1,
  input  Seletor_2,
  output out_5
);

  somador somador_1 ();  // open: A, B, Ci, S, Co
endmodule
